// Logisim project computer_16_v0.circ as structural Verilog: 11 circuits, main circuit zzzIncrement
module secondMain (
);

  wire ADD, ADDI, ADDM, and_2_out, and_3_out, and_4_out, and_5_out, and_6_out, and_7_out, and_8_out,
       and_9_out, and_11_out, ANDD, ANDI, ARITHMITC, BASIC, BOOT, C27, C56, C57, C58, C59, C60, C61, C62,
       C63, CALL, CALL_R, CarryFlag, CF_ADD, CF_C, CF_ROTATE_L, CF_ROTATE_R, CF_SHIFT_L, CF_SHIFT_R, CF_SUB,
       CLAER, CLC, clock_1_out, clock_2_out, clock_3_out, clock_4_out, clock_5_out, clock_6_out, clock_7_out,
       clock_8_out, clock_9_out, clock_10_out, clock_11_out, clock_12_out, clock_13_out, clock_14_out, CLR,
       CMP, CMPI, COMPRISON, DEC, DIV, DIVI, F_HIGH, F_LOW, F_WE, FLOW, HALT, INC, INN, JAE, JB, JE, JG, JL,
       JNE, JUMP, JUMP_R, LDR, LOAD, LOGIC, LOGIC_4bit, LOOPP, MOV, MOVI, MUL, MULI, NOTT, OF_ADD, OF_SUB,
       or_20_out, or_21_out, or_23_out, ORI, ORR, OUTT, OverFlowFlag, Ox3A, Ox3B, Ox37, Ox38, Ox39, POP,
       PUSH, R0_HIGH, R0_LOW, R0_WE, R1_HIGH, R1_LOW, R1_WE, R2_HIGH, R2_LOW, R2_WE, R3_HIGH, R3_LOW, R3_WE,
       R4_HIGH, R4_LOW, R4_WE, R5_HIGH, R5_LOW, R5_WE, R6_HIGH, R6_LOW, R6_WE, RET, ROLI, ROLL, RORI, RORR,
       SHL, SHLI, SHR, SHRI, SignFlag, SP_HIGH, SP_LOW, SP_WE, STOR, STR, SUB, SUBI, SUBM, TEST, TESTI, XCHG,
       xnor_1_out, xor_2_out, XORI, XORR, zzzreasetip_1_reseat;
  wire [2:0] Counter, multiplexer_16_out, zzzincrement_3b_1_outcounter;
  wire [3:0] F_inALU, F_inControl;
  wire [7:0] multiplexer_17_out;
  wire [15:0] ADD_High, AddressBus, AND_High, BOOT_data, DataBus, DataLow, DIV_High, DIV_Low, F_inData,
       F_inHigh, F_inLow, inDataALU1, inDataALU2, IR, MAR_q, MUL_High, MUL_Low, multiplexer_8_out,
       multiplexer_9_out, multiplexer_10_out, multiplexer_11_out, multiplexer_15_out, NOT_High, or_10_out,
       OR_High, outDataALU_1, outDataALU_2, PC_q, R0_inData, R0_inHigh, R0_inLow, R0_outData, R1_inData,
       R1_inHigh, R1_inLow, R1_outData, R2_inData, R2_inHigh, R2_inLow, R2_outData, R3_inData, R3_inHigh,
       R3_inLow, R3_outData, R4_inData, R4_inHigh, R4_inLow, R4_outData, R5_inData, R5_inHigh, R5_inLow,
       R5_outData, R6_inData, R6_inHigh, R6_inLow, R6_outData, RAAM_dout, ROTATE_L_High, ROTATE_R_High,
       SHIFT_L_High, SHIFT_R_High, SP_inData, SP_inHigh, SP_inLow, SP_outData, SUB_High, XOR_High,
       zzzincrement_1_outaddressinstrucre;
  wire [15:4] F_outData;
  wire [63:0] ControlBus, RoomSet;

  ROM #(.addrWidth(16), .dataWidth(16)) u_BOOT (.addr(AddressBus), .data(BOOT_data));
  RAM #(.addrWidth(16), .dataWidth(16), .enables("line")) RAAM (
    .addr(AddressBus), .we(ControlBus[1]), .clk(clock_1_out), .din(DataBus), .dout(RAAM_dout));
  Clock clock_1 (.out(clock_1_out));
  Demultiplexer #(.disabled("Z"), .enable("true"), .select(2), .tristate("true"), .width(16)) demultiplexer_1 (
    .out0(DataBus), .out1(DataLow), .out2(outDataALU_1), .out3(outDataALU_2), .in(RAAM_dout),
    .sel(ControlBus[4:3]), .en(ControlBus[2]));
  assign DataBus = ControlBus[0] ? BOOT_data : 16'bz;  // Controlled_Buffer controlled_buffer_1
  Decoder #(.select(4)) decoder_1 (
    .out0(R0_HIGH), .out1(R1_HIGH), .out2(R2_HIGH), .out3(R3_HIGH), .out4(R4_HIGH), .out5(R5_HIGH),
    .out6(R6_HIGH), .out14(SP_HIGH), .out15(F_HIGH), .sel(ControlBus[59:56]), .en(ControlBus[14]));  // open: out7, out8, out9, out10, out11, out12, out13
  Decoder #(.select(4)) decoder_2 (
    .out0(R0_LOW), .out1(R1_LOW), .out2(R2_LOW), .out3(R3_LOW), .out4(R4_LOW), .out5(R5_LOW), .out6(R6_LOW),
    .out14(SP_LOW), .out15(F_LOW), .sel(ControlBus[63:60]), .en(ControlBus[19]));  // open: out7, out8, out9, out10, out11, out12, out13
  Multiplexer #(.width(16)) multiplexer_1 (.in0(16'h1), .in1(outDataALU_1), .out(inDataALU1), .sel(ControlBus[25]));
  Multiplexer #(.width(16)) multiplexer_2 (.in0(16'h1), .in1(outDataALU_2), .out(inDataALU2), .sel(ControlBus[26]));
  or or_1 (R0_WE, R0_HIGH, R0_LOW);
  or or_2 (R1_WE, R1_HIGH, R1_LOW);
  or or_3 (R2_WE, R2_HIGH, R2_LOW);
  or or_4 (R3_WE, R3_HIGH, R3_LOW);
  or or_5 (R4_WE, R4_HIGH, R4_LOW);
  or or_6 (R5_WE, R5_HIGH, R5_LOW);
  or or_7 (R6_WE, R6_HIGH, R6_LOW);
  or or_8 (SP_WE, SP_HIGH, SP_LOW);
  or or_9 (F_WE, F_HIGH, ControlBus[28], ControlBus[12], F_LOW);
  Multiplexer #(.disabled("Z"), .enable("true"), .select(4), .width(16)) multiplexer_3 (
    .in0(ADD_High), .in1(SUB_High), .in2(MUL_High), .in3(DIV_High), .in4(ADD_High), .in5(SUB_High),
    .in6(AND_High), .in7(OR_High), .in8(XOR_High), .in9(NOT_High), .in10(SHIFT_L_High), .in11(SHIFT_R_High),
    .in12(ROTATE_L_High), .in13(ROTATE_R_High), .in14({16{1'b0}}), .in15({16{1'b0}}), .out(DataBus),
    .sel(ControlBus[35:32]), .en(ControlBus[23]));
  Multiplexer multiplexer_4 (.in0(SignFlag), .in1(F_inControl[1]), .out(F_inALU[1]), .sel(ControlBus[30]));
  Multiplexer multiplexer_5 (.in0(CarryFlag), .in1(CF_C), .out(F_inALU[2]), .sel(ControlBus[30]));
  Multiplexer multiplexer_6 (.in0(OverFlowFlag), .in1(F_inControl[3]), .out(F_inALU[3]), .sel(ControlBus[30]));
  Multiplexer #(.disabled("Z"), .enable("true"), .select(4), .width(16)) multiplexer_7 (
    .in0({16{1'b0}}), .in1({16{1'b0}}), .in2(MUL_Low), .in3(DIV_Low), .in4({16{1'b0}}), .in5({16{1'b0}}),
    .in6({16{1'b0}}), .in7({16{1'b0}}), .in8({16{1'b0}}), .in9({16{1'b0}}), .in10({16{1'b0}}),
    .in11({16{1'b0}}), .in12({16{1'b0}}), .in13({16{1'b0}}), .in14({16{1'b0}}), .in15({16{1'b0}}),
    .out(DataLow), .sel(ControlBus[35:32]), .en(ControlBus[24]));
  Demultiplexer #(.select(2), .tristate("true"), .width(16)) demultiplexer_2 (
    .out0(DataBus), .out1(DataLow), .out2(outDataALU_1), .out3(outDataALU_2), .in(multiplexer_8_out),
    .sel(ControlBus[17:16]));
  Multiplexer #(.disabled("Z"), .enable("true"), .select(4), .width(16)) multiplexer_8 (
    .in0(R0_outData), .in1(R1_outData), .in2(R2_outData), .in3(R3_outData), .in4(R4_outData),
    .in5(R5_outData), .in6(R6_outData), .in14(SP_outData),
    .in15({F_outData, F_inControl[3], CF_C, F_inControl[1:0]}), .out(multiplexer_8_out),
    .sel(ControlBus[59:56]), .en(ControlBus[15]));  // open: in7, in8, in9, in10, in11, in12, in13
  Demultiplexer #(.select(2), .tristate("true"), .width(16)) demultiplexer_3 (
    .out0(DataBus), .out1(DataLow), .out2(outDataALU_1), .out3(outDataALU_2), .in(multiplexer_9_out),
    .sel(ControlBus[22:21]));
  Multiplexer #(.disabled("Z"), .enable("true"), .select(4), .width(16)) multiplexer_9 (
    .in0(R0_outData), .in1(R1_outData), .in2(R2_outData), .in3(R3_outData), .in4(R4_outData),
    .in5(R5_outData), .in6(R6_outData), .in14(SP_outData),
    .in15({F_outData, F_inControl[3], CF_C, F_inControl[1:0]}), .out(multiplexer_9_out),
    .sel(ControlBus[63:60]), .en(ControlBus[20]));  // open: in7, in8, in9, in10, in11, in12, in13
  Multiplexer #(.disabled("Z"), .width(16)) multiplexer_10 (
    .in0(DataBus), .in1(DataLow), .out(multiplexer_10_out), .sel(ControlBus[13]));
  Multiplexer #(.disabled("Z"), .width(16)) multiplexer_11 (
    .in0(DataBus), .in1(DataLow), .out(multiplexer_11_out), .sel(ControlBus[18]));
  Demultiplexer #(.enable("true"), .select(4), .width(16)) demultiplexer_4 (
    .out0(R0_inHigh), .out1(R1_inHigh), .out2(R2_inHigh), .out3(R3_inHigh), .out4(R4_inHigh),
    .out5(R5_inHigh), .out6(R6_inHigh), .out14(SP_inHigh), .out15(F_inHigh), .in(multiplexer_10_out),
    .sel(ControlBus[59:56]), .en(ControlBus[14]));  // open: out7, out8, out9, out10, out11, out12, out13
  Demultiplexer #(.enable("true"), .select(4), .width(16)) demultiplexer_5 (
    .out0(R0_inLow), .out1(R1_inLow), .out2(R2_inLow), .out3(R3_inLow), .out4(R4_inLow), .out5(R5_inLow),
    .out6(R6_inLow), .out14(SP_inLow), .out15(F_inLow), .in(multiplexer_11_out), .sel(ControlBus[63:60]),
    .en(ControlBus[19]));  // open: out7, out8, out9, out10, out11, out12, out13
  Comparator #(.mode("unsigned"), .width(16)) comparator_1 (
    .a(DataBus), .b({16{1'b0}}), .eq(F_inALU[0]));  // open: gt, lt
  Comparator #(.mode("unsigned"), .width(1)) comparator_2 (.a(DataBus[15]), .b(1'b1), .eq(SignFlag));  // open: gt, lt
  assign or_10_out = F_inHigh | F_inLow;  // OR_Gate or_10, 16 bits wide
  Multiplexer #(.select(4)) multiplexer_12 (
    .in0(CF_ADD), .in1(CF_SUB), .in2(1'b0), .in3(1'b0), .in4(CF_ADD), .in5(CF_SUB), .in6(1'b0), .in7(1'b0),
    .in8(CF_SHIFT_L), .in9(CF_SHIFT_R), .in10(CF_ROTATE_L), .in11(CF_ROTATE_R), .in12(1'b0), .in13(1'b0),
    .in14(1'b0), .in15(1'b0), .out(CarryFlag), .sel(ControlBus[35:32]));
  assign R0_inData = R0_inHigh | R0_inLow;  // OR_Gate or_11, 16 bits wide
  assign R1_inData = R1_inHigh | R1_inLow;  // OR_Gate or_12, 16 bits wide
  assign R2_inData = R2_inHigh | R2_inLow;  // OR_Gate or_13, 16 bits wide
  assign R3_inData = R3_inHigh | R3_inLow;  // OR_Gate or_14, 16 bits wide
  assign R4_inData = R4_inHigh | R4_inLow;  // OR_Gate or_15, 16 bits wide
  assign R5_inData = R5_inHigh | R5_inLow;  // OR_Gate or_16, 16 bits wide
  assign R6_inData = R6_inHigh | R6_inLow;  // OR_Gate or_17, 16 bits wide
  assign SP_inData = SP_inHigh | SP_inLow;  // OR_Gate or_18, 16 bits wide
  Multiplexer #(.select(2), .width(16)) multiplexer_13 (
    .in0(or_10_out), .in1({{12{1'b0}}, F_inALU}), .in2({{12{1'b0}}, F_inControl}), .out(F_inData),
    .sel({ControlBus[28], ControlBus[12]}));  // open: in3
  zADD16 zadd16_1 (
    .inALU1(inDataALU1), .inALU2(inDataALU2), .ADD_High(ADD_High), .CF(CF_ADD), .OVF(OF_ADD));  // open: iCF
  zSUB16 zsub16_1 (
    .inALU1(inDataALU1), .inALU2(inDataALU2), .SUB_High(SUB_High), .CF(CF_SUB), .OVF(OF_SUB));  // open: iCF
  Multiplier #(.width(16)) multiplier_1 (.a(inDataALU1), .b(inDataALU2), .out(MUL_High), .cout(MUL_Low));  // open: cin
  Divider #(.width(16)) divider_1 (.a(inDataALU1), .b(inDataALU2), .out(DIV_High), .rem(DIV_Low));  // open: upper
  Register #(.width(16)) R0 (.D(R0_inData), .en(R0_WE), .clk(clock_2_out), .Q(R0_outData));  // open: clr
  Clock clock_2 (.out(clock_2_out));
  Register #(.width(16)) R1 (.D(R1_inData), .en(R1_WE), .clk(clock_3_out), .Q(R1_outData));  // open: clr
  Clock clock_3 (.out(clock_3_out));
  Register #(.width(16)) R2 (.D(R2_inData), .en(R2_WE), .clk(clock_4_out), .Q(R2_outData));  // open: clr
  Clock clock_4 (.out(clock_4_out));
  Register #(.width(16)) R3 (.D(R3_inData), .en(R3_WE), .clk(clock_5_out), .Q(R3_outData));  // open: clr
  Clock clock_5 (.out(clock_5_out));
  Register #(.width(16)) R4 (.D(R4_inData), .en(R4_WE), .clk(clock_6_out), .Q(R4_outData));  // open: clr
  Clock clock_6 (.out(clock_6_out));
  Register #(.width(16)) R5 (.D(R5_inData), .en(R5_WE), .clk(clock_7_out), .Q(R5_outData));  // open: clr
  Clock clock_7 (.out(clock_7_out));
  Register #(.width(16)) R6 (.D(R6_inData), .en(R6_WE), .clk(clock_8_out), .Q(R6_outData));  // open: clr
  Clock clock_8 (.out(clock_8_out));
  Multiplexer #(.select(4)) multiplexer_14 (
    .in0(OF_ADD), .in1(OF_SUB), .in2(1'b0), .in3(1'b0), .in4(OF_ADD), .in5(OF_SUB), .in6(1'b0), .in7(1'b0),
    .in8(1'b0), .in9(1'b0), .in10(1'b0), .in11(1'b0), .in12(1'b0), .in13(1'b0), .in14(1'b0), .in15(1'b0),
    .out(OverFlowFlag), .sel(ControlBus[35:32]));
  zzzIncrement zzzincrement_1 (.inAddressInstrucre(PC_q), .outAddressInstrucre(zzzincrement_1_outaddressinstrucre));
  Multiplexer #(.width(16)) multiplexer_15 (
    .in0(zzzincrement_1_outaddressinstrucre), .in1(DataBus), .out(multiplexer_15_out), .sel(ControlBus[27]));
  Clock clock_9 (.out(clock_9_out));
  assign AND_High = inDataALU1 & inDataALU2;  // AND_Gate and_1, 16 bits wide
  assign OR_High = inDataALU1 | inDataALU2;  // OR_Gate or_19, 16 bits wide
  assign XOR_High = inDataALU1 ^ inDataALU2;  // XOR_Gate xor_1, 16 bits wide
  assign NOT_High = ~inDataALU1;  // NOT_Gate not_1, 16 bits wide
  Register #(.width(16)) PC (
    .D(multiplexer_15_out), .en(ControlBus[8]), .clk(clock_9_out), .Q(PC_q), .clr(ControlBus[7]));
  Register #(.width(16)) MAR (.D(DataBus), .en(ControlBus[10]), .clk(clock_10_out), .Q(MAR_q));  // open: clr
  Clock clock_10 (.out(clock_10_out));
  Register #(.width(16)) SP (.D(SP_inData), .en(SP_WE), .clk(clock_11_out), .Q(SP_outData));  // open: clr
  Clock clock_11 (.out(clock_11_out));
  Register #(.width(16)) FLAGS (
    .D(F_inData), .en(F_WE), .clk(clock_12_out), .Q({F_outData, F_inControl[3], CF_C, F_inControl[1:0]}));  // open: clr
  Clock clock_12 (.out(clock_12_out));
  zSHIFT_L zshift_l_1 (.inALU1(inDataALU1), .inALU2(inDataALU2), .CF(CF_SHIFT_L), .result(SHIFT_L_High));
  zSHIFT_R zshift_r_1 (.inALU1(inDataALU1), .inALU2(inDataALU2), .CF(CF_SHIFT_R), .result(SHIFT_R_High));
  zROTATE_L zrotate_l_1 (.inALU1(inDataALU1), .inALU2(inDataALU2), .CF(CF_ROTATE_L), .result(ROTATE_L_High));
  zROTATE_R zrotate_r_1 (.inALU1(inDataALU1), .inALU2(inDataALU2), .CF(CF_ROTATE_R), .result(ROTATE_R_High));
  assign AddressBus = ControlBus[11] ? MAR_q : 16'bz;  // Controlled_Buffer controlled_buffer_2
  Demultiplexer #(.disabled("Z"), .enable("true"), .tristate("true"), .width(16)) demultiplexer_6 (
    .out0(AddressBus), .out1(DataBus), .in(PC_q), .sel(ControlBus[29]), .en(ControlBus[9]));
  Decoder #(.enable("false"), .select(6)) decoder_3 (
    .out0(BOOT), .out1(LOAD), .out2(STOR), .out3(LDR), .out4(STR), .out5(MOV), .out6(MOVI), .out7(PUSH),
    .out8(POP), .out9(XCHG), .out10(INN), .out11(OUTT), .out12(ADD), .out13(ADDI), .out14(ADDM), .out15(SUB),
    .out16(SUBI), .out17(SUBM), .out18(MUL), .out19(MULI), .out20(DIV), .out21(DIVI), .out22(INC),
    .out23(DEC), .out24(ANDD), .out25(ANDI), .out26(ORR), .out27(ORI), .out28(XORR), .out29(XORI),
    .out30(NOTT), .out31(SHL), .out32(SHLI), .out33(SHR), .out34(SHRI), .out35(ROLL), .out36(ROLI),
    .out37(RORR), .out38(RORI), .out39(CMP), .out40(CMPI), .out41(TEST), .out42(TESTI), .out43(JUMP),
    .out44(JUMP_R), .out45(JE), .out46(JNE), .out47(JB), .out48(JAE), .out49(JG), .out50(JL), .out51(CALL),
    .out52(CALL_R), .out53(RET), .out54(LOOPP), .out55(Ox37), .out56(Ox38), .out57(Ox39), .out58(Ox3A),
    .out59(Ox3B), .out60(CLC), .out61(F_inControl[2]), .out62(CLR), .out63(HALT), .sel(IR[5:0]));
  Multiplexer #(.width(3)) multiplexer_16 (
    .in0(zzzincrement_3b_1_outcounter), .in1(3'b000), .out(multiplexer_16_out), .sel(zzzreasetip_1_reseat));
  zzzIncrement_3b zzzincrement_3b_1 (.inCounter(Counter), .outCounter(zzzincrement_3b_1_outcounter));
  Register #(.width(16)) u_IR (.D(DataBus), .en(ControlBus[5]), .clk(clock_13_out), .Q(IR));  // open: clr
  Clock clock_13 (.out(clock_13_out));
  Register #(.width(3)) u_Counter (.D(multiplexer_16_out), .clk(clock_14_out), .Q(Counter));  // open: en, clr
  Clock clock_14 (.out(clock_14_out));
  zzzReasetIP zzzreasetip_1 (.inDataBus(DataBus), .cReseat(ControlBus[6]), .Reseat(zzzreasetip_1_reseat));
  ROM #(.addrWidth(9), .dataWidth(64)) Opcode (.addr({IR[5:0], Counter}), .data(RoomSet));
  xnor xnor_1 (xnor_1_out, F_inControl[3], F_inControl[1]);
  xor xor_2 (xor_2_out, F_inControl[3], F_inControl[1]);
  Comparator #(.mode("unsigned"), .width(9)) comparator_3 (
    .a({9{1'b0}}), .b({XCHG, POP, PUSH, MOVI, MOV, STR, LDR, STOR, LOAD}), .lt(BASIC));  // open: gt, eq
  Comparator #(.mode("unsigned"), .width(12)) comparator_4 (
    .a({12{1'b0}}), .b({DEC, INC, DIVI, DIV, MULI, MUL, SUBM, SUBI, SUB, ADDM, ADDI, ADD}), .lt(ARITHMITC));  // open: gt, eq
  and and_2 (and_2_out, JE, F_inControl[0]);
  and and_3 (and_3_out, JNE, ~F_inControl[0]);  // AND_Gate
  and and_4 (and_4_out, JB, CF_C);
  and and_5 (and_5_out, JAE, ~CF_C);  // AND_Gate
  and and_6 (and_6_out, JG, and_7_out);
  and and_7 (and_7_out, ~F_inControl[0], xnor_1_out);  // AND_Gate
  and and_8 (and_8_out, JL, xor_2_out);
  or or_20 (or_20_out, or_21_out, FLOW);
  or or_21 (or_21_out, BASIC, ARITHMITC, LOGIC, COMPRISON);
  Comparator #(.mode("unsigned"), .width(4)) comparator_5 (
    .a(4'b0000), .b({HALT, CLR, F_inControl[2], CLC}), .lt(CLAER));  // open: gt, eq
  Comparator #(.mode("unsigned"), .width(4)) comparator_6 (
    .a(4'b0000), .b({RORI, ROLI, SHRI, SHLI}), .lt(LOGIC_4bit));  // open: gt, eq
  or or_22 (C27, and_9_out, and_11_out);
  and and_9 (and_9_out, or_23_out, ~Counter[0]);  // AND_Gate
  or or_23 (or_23_out, and_2_out, and_3_out, and_4_out, and_5_out, and_6_out, and_8_out);
  assign outDataALU_2 = LOGIC_4bit ? {{12{1'b0}}, IR[13:10]} : 16'bz;  // Controlled_Buffer controlled_buffer_3
  assign {C63, C62, C61, C60, C59, C58, C57, C56} = IR[13:6] & multiplexer_17_out;  // AND_Gate and_10, 8 bits wide
  Multiplexer #(.width(8)) multiplexer_17 (.in0({8{1'b0}}), .in1({8{1'b1}}), .out(multiplexer_17_out), .sel(or_20_out));
  and and_11 (and_11_out, ~F_inControl[0], Counter[0], LOOPP);  // AND_Gate
  Comparator #(.mode("unsigned"), .width(3)) comparator_7 (
    .a(3'b000), .b({TEST, CMPI, CMP}), .lt(COMPRISON));  // open: gt, eq
  Comparator #(.mode("unsigned"), .width(12)) comparator_8 (
    .a({12{1'b0}}), .b({LOOPP, RET, CALL_R, CALL, JL, JG, JAE, JB, JNE, JE, JUMP_R, JUMP}), .lt(FLOW));  // open: gt, eq
  Comparator #(.mode("unsigned"), .width(12)) comparator_9 (
    .a({12{1'b0}}), .b({LOGIC_4bit, RORR, ROLL, SHR, SHL, NOTT, XORI, XORR, ORI, ORR, ANDI, ANDD}), .lt(LOGIC));  // open: gt, eq
  or or_24 (ControlBus[0], RoomSet[0], 1'b0);
  or or_25 (ControlBus[1], RoomSet[1], 1'b0);
  or or_26 (ControlBus[2], RoomSet[2], 1'b0);
  or or_27 (ControlBus[3], RoomSet[3], 1'b0);
  or or_28 (ControlBus[4], RoomSet[4], 1'b0);
  or or_29 (ControlBus[5], RoomSet[5], 1'b0);
  or or_30 (ControlBus[6], RoomSet[6], 1'b0);
  or or_31 (ControlBus[7], RoomSet[7], 1'b0);
  or or_32 (ControlBus[8], RoomSet[8], 1'b0);
  or or_33 (ControlBus[9], RoomSet[9], 1'b0);
  or or_34 (ControlBus[10], RoomSet[10], 1'b0);
  or or_35 (ControlBus[11], RoomSet[11], 1'b0);
  or or_36 (ControlBus[12], RoomSet[12], 1'b0);
  or or_37 (ControlBus[13], RoomSet[13], 1'b0);
  or or_38 (ControlBus[14], RoomSet[14], 1'b0);
  or or_39 (ControlBus[15], RoomSet[15], 1'b0);
  or or_40 (ControlBus[16], RoomSet[16], 1'b0);
  or or_41 (ControlBus[17], RoomSet[17], 1'b0);
  or or_42 (ControlBus[18], RoomSet[18], 1'b0);
  or or_43 (ControlBus[19], RoomSet[19], 1'b0);
  or or_44 (ControlBus[20], RoomSet[20], 1'b0);
  or or_45 (ControlBus[21], RoomSet[21], 1'b0);
  or or_46 (ControlBus[22], RoomSet[22], 1'b0);
  or or_47 (ControlBus[23], RoomSet[23], 1'b0);
  or or_48 (ControlBus[24], RoomSet[24], 1'b0);
  or or_49 (ControlBus[25], RoomSet[25], 1'b0);
  or or_50 (ControlBus[26], RoomSet[26], 1'b0);
  or or_51 (ControlBus[27], RoomSet[27], C27);
  or or_52 (ControlBus[28], RoomSet[28], 1'b0);
  or or_53 (ControlBus[29], RoomSet[29], 1'b0);
  or or_54 (ControlBus[30], RoomSet[30], 1'b0);
  or or_55 (ControlBus[31], RoomSet[31], 1'b0);
  or or_56 (ControlBus[32], RoomSet[32], 1'b0);
  or or_57 (ControlBus[33], RoomSet[33], 1'b0);
  or or_58 (ControlBus[34], RoomSet[34], 1'b0);
  or or_59 (ControlBus[35], RoomSet[35], 1'b0);
  or or_60 (ControlBus[36], RoomSet[36], 1'b0);
  or or_61 (ControlBus[37], RoomSet[37], 1'b0);
  or or_62 (ControlBus[38], RoomSet[38], 1'b0);
  or or_63 (ControlBus[39], RoomSet[39], 1'b0);
  or or_64 (ControlBus[40], RoomSet[40], 1'b0);
  or or_65 (ControlBus[41], RoomSet[41], 1'b0);
  or or_66 (ControlBus[42], RoomSet[42], 1'b0);
  or or_67 (ControlBus[43], RoomSet[43], 1'b0);
  or or_68 (ControlBus[44], RoomSet[44], 1'b0);
  or or_69 (ControlBus[45], RoomSet[45], 1'b0);
  or or_70 (ControlBus[46], RoomSet[46], 1'b0);
  or or_71 (ControlBus[47], RoomSet[47], 1'b0);
  or or_72 (ControlBus[48], RoomSet[48], 1'b0);
  or or_73 (ControlBus[49], RoomSet[49], 1'b0);
  or or_74 (ControlBus[50], RoomSet[50], 1'b0);
  or or_75 (ControlBus[51], RoomSet[51], 1'b0);
  or or_76 (ControlBus[52], RoomSet[52], 1'b0);
  or or_77 (ControlBus[53], RoomSet[53], 1'b0);
  or or_78 (ControlBus[54], RoomSet[54], 1'b0);
  or or_79 (ControlBus[55], RoomSet[55], 1'b0);
  or or_80 (ControlBus[56], RoomSet[56], C56);
  or or_81 (ControlBus[57], RoomSet[57], C57);
  or or_82 (ControlBus[58], RoomSet[58], C58);
  or or_83 (ControlBus[59], RoomSet[59], C59);
  or or_84 (ControlBus[60], RoomSet[60], C60);
  or or_85 (ControlBus[61], RoomSet[61], C61);
  or or_86 (ControlBus[62], RoomSet[62], C62);
  or or_87 (ControlBus[63], RoomSet[63], C63);

  // Other names for the same wires on the sheet: JZ = JE; JNZ = JNE; JC = JB; JNC = JAE; ZeroFlag = F_inALU[0];
  //   F_outData[3:0] = {F_inControl[3], CF_C, F_inControl[1:0]}; ZF_C = F_inControl[0]; SF_C = F_inControl[1];
  //   STC = F_inControl[2]; VF_C = F_inControl[3]

  // Notes on the sheet:
  //   contents of BOOT (hex, n*v repeats v):
  //   186 6 6 1234 28 1234 2e 1b4 186 5 45 67 2e 1b4 186 2 2 800 186 1 81 800 a7 2e 1b4 c6 810 186 4 c4 4
  //   186 3 d03 4 127 2e 1b4 386 1ff 186 7 387 186 8 3948 167 2e 1b4 186 9 6 aaaa 46 5555 409 28 5555 2e
  //   1b4 186 c 6 a 46 5 40c 28 f 2e 1b4 186 d d 5 28 14 2e 1b4 186 e 402 820 e 820 28 19 2e 1b4 186 f 40f
  //   28 14 2e 1b4 186 10 10 5 28 f 2e 1b4 186 11 11 820 28 a 2e 1b4 186 12 6 6 46 7 412 28 2a 2e 1b4 186
  //   13 13 2 28 54 2e 1b4 186 14 6 54 46 2 414 28 2a 2e 1b4 186 15 15 7 28 6 2e 1b4 186 16 16 28 7 2e 1b4
  //   186 17 17 28 6 2e 1b4 186 18 6 123 46 f0 418 28 20 2e 1b4 186 19 19 f0 28 20 2e 1b4 186 1a 46 f00
  //   41a 28 f20 2e 1b4 186 1b 1b f 28 f2f 2e 1b4 186 1c 46 f00 41c 28 2f 2e 1b4 186 1d 1d 20 28 f 2e 1b4
  //   186 1e 6 f0f 1e 28 f0f0 2e 1b4 186 1f 6 1 46 4 41f 28 10 2e 1b4 186 20 1020 28 100 2e 1b4 186 21 421
  //   28 10 2e 1b4 186 22 1022 28 1 2e 1b4 186 23 6 f000 46 4 423 28 f 2e 1b4 186 24 1024 28 f0 2e 1b4 186
  //   25 425 28 f 2e 1b4 186 26 1026 28 f000 2e 1b4 186 27 6 a 46 a 427 2e 1b4 186 28 28 a 2e 1b4 186 29 6
  //   ff 46 f0 429 2d 1b4 186 2a 6 ff 2a f 2d 1b4 186 2b 2b 148 2b 1b4 186 2c 6 14f 2c 2b 1b4 186 2d 6 0
  //   28 0 2d 159 2b 1b4 186 2e 6 5 28 0 2e 163 2b 1b4 186 2f 3d 2f 16a 2b 1b4 186 30 3c 30 171 2b 1b4 186
  //   31 6 a 46 5 427 31 17c 2b 1b4 186 32 67 32 183 2b 1b4 186 33 3b3 18f 186 34 6 192 3b4 0 2b 193 186
  //   35 3835 3835 186 36 6 0 86 3 16 b6 199 28 3 2e 1b4 186 3c 3c 186 3d 3d 186 3e 6 1234 3e 28 0 2e 1b4
  //   146 1 186 0 3f 146 bad0 3f ffff
  //   0
  //   0
  //   0
  //   0
  //   0
  //   0
  //   0
  //   0
  //   0
  //   0
  //   0
  //   0
  //   OF
  //   CF
  //   SF
  //   ZF
  //   contents of Opcode (hex, n*v repeats v):
  //   343 80 364 5*0 704 4804 364 5*0 704 100802 364 5*0 6d0071c 4804 364 5*0 682871c 100802 364 5*0
  //   104000 364 6*0 4304 364 6*0 50282c400 100802 364 5*0 100400 402d8680c 364 5*0 1dc000 364 22*0
  //   6f2d000 364 6*0 682d31c 364 6*0 704 682d81c 364 5*0 106f2d000 364 6*0 10682d31c 364 6*0 704
  //   10682d81c 364 5*0 207fed000 364 6*0 2078ec31c 364 6*0 307fed000 364 6*0 3078ec31c 364 6*0 40282d000
  //   364 6*0 50282d000 364 6*0 606f2d000 364 6*0 60682d31c 364 6*0 706f2d000 364 6*0 70682d31c 364 6*0
  //   806f2d000 364 6*0 80682d31c 364 6*0 90282d000 364 6*0 a06f2d000 364 6*0 a0682d000 364 6*0 b06f2d000
  //   364 6*0 b0682d000 364 6*0 c06f2d000 364 6*0 c0682d000 364 6*0 d06f2d000 364 6*0 d0682d000 364 6*0
  //   106f29000 364 6*0 10682931c 364 6*0 606f29000 364 6*0 60682931c 364 6*0 8000304 364 6*0 100100 364
  //   6*0 304 364 6*0 304 364 6*0 304 364 6*0 304 364 6*0 304 364 6*0 304 364 6*0 50282c400 20000a02
  //   8000304 364 4*0 50282c400 20000a02 8100100 364 4*0 100400 8000904 402d80100 364 4*0 54282d000 304
  //   364 45*0 10000364 7*0 10000364 7*0 f00804000 364
endmodule

module zzzIncrement (
  input  [15:0] inAddressInstrucre,
  output [15:0] outAddressInstrucre
);

  Adder #(.width(16)) adder_1 (.a(inAddressInstrucre), .b(16'h1), .out(outAddressInstrucre));  // open: cin, cout
endmodule

module zzzIncrement_3b (
  input  [2:0] inCounter,
  output [2:0] outCounter
);

  Adder #(.width(3)) adder_1 (.a(inCounter), .b(3'b001), .out(outCounter));  // open: cin, cout
endmodule

module zzzReasetIP (
  input  [15:0] inDataBus,
  input  cReseat,
  output Reseat
);

  wire and_1_out, clock_1_out, clock_2_out, comparator_1_eq, register_1_q, register_2_q;

  Comparator #(.mode("unsigned"), .width(16)) comparator_1 (
    .a(inDataBus), .b({16{1'b1}}), .eq(comparator_1_eq));  // open: gt, lt
  Register #(.width(1)) register_1 (.D(1'b1), .en(comparator_1_eq), .clk(clock_1_out), .Q(register_1_q));  // open: clr
  Clock clock_1 (.out(clock_1_out));
  Register #(.width(1)) register_2 (.D(register_1_q), .clk(clock_2_out), .Q(register_2_q));  // open: en, clr
  Clock clock_2 (.out(clock_2_out));
  and and_1 (and_1_out, comparator_1_eq, ~register_2_q);  // AND_Gate
  and and_2 (Reseat, ~and_1_out, cReseat);  // AND_Gate
endmodule

module zADD16 (
  input  [15:0] inALU1,
  input  [15:0] inALU2,
  input  iCF,
  output [15:0] ADD_High,
  output CF,
  output OVF
);

  wire xnor_1_out, xor_1_out;

  xnor xnor_1 (xnor_1_out, inALU2[15], inALU1[15]);
  xor xor_1 (xor_1_out, inALU1[15], ADD_High[15]);
  Adder #(.width(16)) adder_1 (.a(inALU1), .b(inALU2), .out(ADD_High), .cin(iCF), .cout(CF));
  and and_1 (OVF, xnor_1_out, xor_1_out);
endmodule

module zSUB16 (
  input  [15:0] inALU1,
  input  [15:0] inALU2,
  input  iCF,
  output [15:0] SUB_High,
  output CF,
  output OVF
);

  wire xor_1_out, xor_2_out;

  xor xor_1 (xor_1_out, inALU2[15], inALU2[15]);
  and and_1 (OVF, xor_1_out, xor_2_out);
  Subtractor #(.width(16)) subtractor_1 (.a(inALU1), .b(inALU2), .out(SUB_High), .bin(iCF), .bout(CF));
  xor xor_2 (xor_2_out, inALU2[15], SUB_High[15]);
endmodule

module zSHIFT_L (
  input  [15:0] inALU1,
  input  [15:0] inALU2,
  output CF,
  output [15:0] result
);

  Shifter #(.width(17)) shifter_1 (.in({1'b0, inALU1}), .\dist ({1'b0, inALU2[3:0]}), .out({CF, result}));
endmodule

module zSHIFT_R (
  input  [15:0] inALU1,
  input  [15:0] inALU2,
  output CF,
  output [15:0] result
);

  Shifter #(.shift("lr"), .width(17)) shifter_1 (.in({inALU1, 1'b0}), .\dist ({1'b0, inALU2[3:0]}), .out({result, CF}));
endmodule

module zROTATE_L (
  input  [15:0] inALU1,
  input  [15:0] inALU2,
  output CF,
  output [15:0] result
);

  Shifter #(.shift("rl"), .width(16)) shifter_1 (.in(inALU1), .\dist (inALU2[3:0]), .out({result[15:1], CF}));

  assign result[0] = CF;
endmodule

module zROTATE_R (
  input  [15:0] inALU1,
  input  [15:0] inALU2,
  output CF,
  output [15:0] result
);

  Shifter #(.shift("rr"), .width(16)) shifter_1 (.in(inALU1), .\dist (inALU2[3:0]), .out({CF, result[14:0]}));

  assign result[15] = CF;
endmodule

module test (
  input  [3:0] Data,
  input  B0,
  input  B1,
  input  B2,
  input  B3,
  input  S1,
  input  S0,
  output out_8
);

  wire and_1_out, and_2_out, and_3_out, and_4_out, and_5_out, and_6_out, and_7_out, and_8_out, clock_1_out,
       clock_2_out, clock_3_out, not_1_out, not_2_out;
  wire [3:0] adder_1_out, adder_2_out, AX_q, BX_q, Counter_q, IR_q, MAR_q, multiplexer_1_out, rom_1_data;

  Register #(.width(4)) IR (.Q(IR_q));  // open: D, en, clk, clr
  Register #(.width(4)) Counter (.D(adder_1_out), .clk(clock_1_out), .Q(Counter_q));  // open: en, clr
  Clock clock_1 (.out(clock_1_out));
  Adder #(.width(4)) adder_1 (.a(4'b0001), .b(Counter_q), .out(adder_1_out));  // open: cin, cout
  Register #(.width(4)) MAR (.Q(MAR_q));  // open: D, en, clk, clr
  ROM #(.dataWidth(4)) rom_1 (.addr({IR_q, Counter_q}), .data(rom_1_data));
  not not_1 (not_1_out, S1);
  not not_2 (not_2_out, S0);
  Multiplexer #(.select(2), .width(4)) multiplexer_1 (
    .in0(AX_q), .in1(BX_q), .in2(Data), .in3(adder_2_out), .out(multiplexer_1_out), .sel(rom_1_data[3:2]));
  and and_1 (and_1_out, not_2_out, not_1_out);
  and and_2 (and_2_out, S0, not_1_out);
  and and_3 (and_3_out, not_2_out, S1);
  and and_4 (and_4_out, S0, S1);
  Register #(.width(4)) AX (.D(multiplexer_1_out), .en(rom_1_data[0]), .clk(clock_2_out), .Q(AX_q));  // open: clr
  Clock clock_2 (.out(clock_2_out));
  Register #(.width(4)) BX (.D(multiplexer_1_out), .en(rom_1_data[1]), .clk(clock_3_out), .Q(BX_q));  // open: clr
  Clock clock_3 (.out(clock_3_out));
  and and_5 (and_5_out, B0, and_1_out);
  and and_6 (and_6_out, B1, and_2_out);
  and and_7 (and_7_out, B2, and_3_out);
  and and_8 (and_8_out, B3, and_4_out);
  or or_1 (out_8, and_5_out, and_6_out, and_7_out, and_8_out);
  Adder #(.width(4)) adder_2 (.a(AX_q), .b(BX_q), .out(adder_2_out));  // open: cin, cout

  // Notes on the sheet:
  //   contents of rom_1 (hex, n*v repeats v):
  //   5 9 e
endmodule
